# Fritzing sketch schéma électronique accélérometre (saved by Fritzing 0.9.3b)
breadboards: 1

parts:
  Composant1 = Triple Axis Accelerometer Breakout - ADXL345
  M1 = DOIT Esp32 DevKit v1 (30 pins long, 11 pins width) [part_number=ESP32S-PIN30]

nets:
  N1: Composant1.GADXL345, M1.GND
  VCC: Composant1.VCC, M1.3V3
  N2: Composant1.CS, M1.D15
  N3: Composant1.SDO, M1.D12
  N4: Composant1.SDA, M1.D13
  N5: Composant1.SCL, M1.D14

custom parts:
  Triple Axis Accelerometer Breakout - ADXL345: Description: This new version adds 2 standoff holes as well as an extra decoupling capacitor. The ADXL345 is a small, thin, low power, 3-axis accelerometer with high resolution (13-bit) measurement at up to ±16 g. Digital output data is formatted as 16-bit twos complement and is accessible through either a SPI (3- or 4-wire) or I2C digital interface. The ADXL345 is well suited to measures the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
  DOIT Esp32 DevKit v1 (30 pins long, 11 pins width): The DOIT Esp32 DevKit v1 is one of the development board created by DOIT to evaluate the ESP-WROOM-32 module. It is based on the ESP32 microcontroller that boasts Wifi, Bluetooth, Ethernet and Low Power support all in a single chip. (vanepp) made breadboard work, adjusted pin numbering and labels and reduced size of schematic and cleaned up pcb. This chip is 30pins long (2 x15) and 11 pins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
