# Fritzing sketch schéma électronique complet (saved by Fritzing 0.9.3b)
breadboards: 1

parts:
  M1 = DOIT Esp32 DevKit v1 (30 pins long, 11 pins width) [part_number=ESP32S-PIN30]
  U2 = GP-2106 [package=gp-2106]
  M3 = BME280
  Composant2 = Adafruit MMA8451 Accelerometer [part_number="Adafruit #2019"]

nets:
  VIN: M1.3V3, U2.1PPS, U2.VCC, M3.VIN, Composant2.VIN
  GND: M1.GND, U2.GND, U2.ONOFF, M3.GND, Composant2.GND
  N1: M1.RX2, U2.TX
  N2: M1.TX2, U2.RX
  N3: M1.D21, M3.SDA, Composant2.SDA
  N4: M1.D22, M3.SCL, Composant2.SCL

notes:
  Accéléromètre - I2C
  adresse: 0x1D (default)
  Temperature - I2C
  adresse:
  Wisol Sigfox - RX/TX

custom parts:
  DOIT Esp32 DevKit v1 (30 pins long, 11 pins width): The DOIT Esp32 DevKit v1 is one of the development board created by DOIT to evaluate the ESP-WROOM-32 module. It is based on the ESP32 microcontroller that boasts Wifi, Bluetooth, Ethernet and Low Power support all in a single chip. (vanepp) made breadboard work, adjusted pin numbering and labels and reduced size of schematic and cleaned up pcb. This chip is 30pins long (2 x15) and 11 pins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
  BME280: Temperature Humidity Barometric presure Sensor
  Adafruit MMA8451 Accelerometer: So many accelerometers and so little time! We've expanded our accelerometer selection even more with this high-precision and inexpensive MMA8451 Triple-Axis Accelerometer w/ 14-bit ADC. You can detect motion, tilt and basic orientation with a digital accelerometer - and the MMA8451 is a great accelerometer to start with. It has a wide usage range, from +-2g up to +-8g yet is easy to use with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
